# Fritzing sketch BB_Arduino_UART_testing (saved by Fritzing 0.9.3b)
breadboards: 1

parts:
  Part1 = Arduino Mega 2560 (Rev3)
  BeagleBone1 = BeagleBone Black
  Part3 = Adafruit 4-channel I2C-safe Bi-directional Logic Level Converter [part_number="Adafruit #757"]

nets:
  N1: Part1.D19/RX1, Part3.B2
  N2: Part1.D18/TX1, Part3.B1
  N3: Part1.5V, Part3.HV
  GND: Part1.GND, BeagleBone1.no_name_yet#1, Part3.GND
  N4: BeagleBone1.no_name_yet#3, Part3.LV
  N5: BeagleBone1.no_name_yet#11, BeagleBone1.no_name_yet#22, BeagleBone1.no_name_yet#26, BeagleBone1.no_name_yet#138, Part3.A1
  N6: BeagleBone1.no_name_yet#24, Part3.A2

custom parts:
  BeagleBone Black: BeagleBone Black rev. A5B
  Adafruit 4-channel I2C-safe Bi-directional Logic Level Converter: Because the Arduino (and Basic Stamp) are 5V devices, and most modern sensors, displays, flash cards and modes are 3.3V-only, many makers find that they need to perform level shifting/conversion to protect the 3.3V device from 5V. We do have some other handy level shifters in the shop, from the DIP 74LVC245 to the fancy bi-directional TXB0108. However, neither of these are happy to work with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
